# Fritzing sketch Esquematico (saved by Fritzing 0.9.3b)
breadboards: 1

parts:
  NodeMCU1 = NodeMCU V1.0 [part_number=A]
  Mod1 = KY-015 Temperature & Humidity Sensor Module [package="Breakout board"]
  LED1 = LEDs [package=led10mm]
  R1 = Resistor [tolerance=±5% resistance=220 package="1206 [SMD]"]
  KY-1 = Keyes Relay [package=THT]

nets:
  N1: NodeMCU1.D1, KY-1.ground
  N2: NodeMCU1.3V3, Mod1.-, KY-1.signal, KY-1.NO
  N3: NodeMCU1.GND, Mod1.S, R1.Pin_0, KY-1.power
  N4: NodeMCU1.D5, Mod1.Vin
  N5: LED1.C, R1.Pin_1
  N6: LED1.A, KY-1.C

custom parts:
  NodeMCU V1.0: ESP8266 based NodeMCU
  KY-015 Temperature & Humidity Sensor Module: KY-015 temperature and humidity sensor module, provides a low-latency serial interface to measure humidity and temperature.
  Keyes Relay: The Keyes 5V relay module is suitable for SCM development, home appliance control. It uses a 5V~12V TIL control signal which can control DC / AC signal.

// code stored in the sketch: ESP_Telegram.ino
#include <DHT.h>

#include <UniversalTelegramBot.h>
#include <ESP8266WiFi.h>
#include <WiFiClientSecure.h>
#include <NTPClient.h>
#include <WiFiUdp.h>


char ssid[] = "Samsung-Direct-N92I020";  // nome do seu roteador WIFI (SSID)
char password[] = "1234567890"; // senha do roteador WIFI

#define BOT_TOKEN "1791417002:AAGOOcfdZ9A3psMofvi-rQ2CipOeqfsEVMs"  // sua chave Token Bot Telegram
// Para obter o Chat ID, acesse Telegram => usuario IDBot => comando /getid


// cliente SSL necessario para a Biblioteca
WiFiClientSecure client;
//Objeto para comunicação pelo Telegram
UniversalTelegramBot bot(BOT_TOKEN, client);

uint32_t lastCheckTime = 0; //Tempo em que foi feita a última checagem

#define SENDER_ID_COUNT 3 //Quantidade de usuários que podem interagir com o bot
//IDs dos usuários que podem interagir com o bot.
String ID_Ramon = "1159192127";
String ID_Aryon = "1888341656";
String ID_Gabriel = "1247734721";
String validSenderIds[SENDER_ID_COUNT] = {ID_Ramon, ID_Aryon, ID_Gabriel};

int Bot_mtbs = 900; //tempo médio entre varredura de mensagens
//long Bot_lasttime;   //última vez que a varredura de mensagens foi feita

String ChatIdPadrao = "xxxxxxxxxxxx";

// Variaveis
#define Chuva_D D0 // Pino digital do sensor de chuva
#define Chuva_A A0 // Pino Analogico do sensor de chuva

#define Presenca 4 // Pino Sensor de presença

#define Buzzer 15 // Pino Buzzer

#define Rele 5 // Pino modulo Relé

#define DHTPIN 14 // Pino Sensor DHT11 (Temp & Umid)
#define DHTTYPE DHT11 // DHT 11
DHT dht(DHTPIN, DHTTYPE);

void setup() {
  Serial.begin(115200);

  //Inicializa o WiFi e se conecta à rede
  setupWiFi();

  // Inicializa as entradas e saidas
  pinMode(Rele, OUTPUT); //Relé 1
  digitalWrite(Rele, HIGH);

  pinMode(LED_BUILTIN, OUTPUT); // LED da placa
  digitalWrite(LED_BUILTIN, HIGH);

  /*
  pinMode(Chuva_D, INPUT); //Sensor de Chuva DIGITAL
  //pinMode(Chuva_A, INPUT); //Sensor de Chuva ANALOGICO

  pinMode(Presenca, INPUT); //Sensor de presença

  pinMode(Buzzer, OUTPUT); //Buzzer
  */
  
  //Inicializa sensor de temperatura e umidade relativa do ar
  dht.begin();
  
  Serial.println("\nControle ativo! ");
  bot.sendMessage(ID_Ramon, "Controle Ativo!", "HTML");
}

void setupWiFi() {
  // Inicializa conexão Wifi
  WiFi.mode(WIFI_AP_STA);   // Configura o WIFI para modo estação e Acess point
  WiFi.disconnect();        // desconecta o WIFI
  delay(500);               // atraso de 500 milisegundos

  Serial.print("Conectando à rede " + String(ssid));
  WiFi.begin(ssid, password);

  // Enquanto não estiver conectado ao WiFi
  while (WiFi.status() != WL_CONNECTED) // aguardando a conexão WEB
  {
    digitalWrite(LED_BUILTIN, LOW);
    delay(50);
    digitalWrite(LED_BUILTIN, HIGH);
    delay(50);
  }

  //Se chegou aqui está conectado
  delay(800);
  Serial.println();
  Serial.println("Conectado!");
  Serial.print("IP da conexão: ");
  Serial.println(WiFi.localIP());

  // Conecta cliente com SSL
  client.setFingerprint("F2:AD:29:9C:34:48:DD:8D:F4:CF:52:32:F6:57:33:68:2E:81:C1:90");
  while (!client.connect("api.telegram.org", 443))
  {
    digitalWrite(LED_BUILTIN, LOW);
    delay(200);
    digitalWrite(LED_BUILTIN, HIGH);
    delay(200);
  }
}

void handleNewMessages(int numNewMessages)
{
  String answer;
  
  for (int i = 0; i < numNewMessages; i++) //para cada mensagem nova
  {
    String chatId = String(bot.messages[i].chat_id); //id do chat
    String senderId = String(bot.messages[i].from_id); //id do Contato
    
    String text = bot.messages[i].text; //texto que chegou
    String from_name = bot.messages[i].from_name; //Nome do Contato

    Serial.println("ID: " + chatId + " \tNome: " + from_name);

    //Serial.println("senderId: " + senderId); //mostra no monitor serial o id de quem mandou a mensagem

    boolean validSender = validateSender(senderId); //verifica se é o id de um remetente da lista de remetentes válidos

    if (!validSender) //se não for um remetente válido
    {
      answer = "Desculpe, mas você não tem permissão! Fale com o admin desse bot (@ramon1357) para conseguir a permição.";
      bot.sendMessage(chatId, answer, "HTML"); //envia mensagem que não possui permissão e retorna sem fazer mais nada
      continue; //continua para a próxima iteração do for (vai para próxima mensagem, não executa o código abaixo)
    }

    /*String text = bot.messages[i].text; //texto que chegou
    String from_name = bot.messages[i].from_name; //Nome do Contato*/
    
    Serial.println("Recebido de " + from_name + ": " + text);

    /*
    if(Chuva_D == LOW){
      answer = "Opa! \n🌨 Está chovendo.";
      Serial.println(answer);
      bot.sendMessage(ID_Ramon, answer, "Markdown");
    }*/

    if(text == "/start" || text == "start" || text == "Start" || text == "/Start")  {
      answer = "Sejá Bem Vindo **Sr(a) " + from_name + "!** \nO bot já está iniciado.\n\n";
      answer += "Digite /Comandos para saber os comandos disponiveis.";
    }
    else if(text == "Status" || text == "/Status"){
      answer = "Sistema no AR! \n";
      answer +="Está tudo bem por aqui, obrigado por perguntar! 👍";
    }
    else if(text == "Ajuda" || text == "/Ajuda") {
      answer = "Precisando de Ajuda? \nEntre em contato com o ADMIN(@ramon1357) deste BOT.";
    }
    else if(text == "Comandos" || text == "/Comandos") {
      answer = "/start ou **start** \n__Descrição:__ Inicia o chat do bot. _(Comando não obrigatorio)_ \n\n";
      answer += "/Status ou **Status** \n**Descrição:** Retorna o status do bot. \n\n";
      answer += "/Ajuda ou **Ajuda** \n**Descrição:** Mais informação e contato para ajuda. \n\n";
      answer += "/Comandos ou **Comandos** \n**Descrição:** Retorna todos os possiveis comandos. \n\n";
      answer += "/Ligar ou **Ligar** \n**Descrição:** Liga a luz. \n\n";
      answer += "/Desligar ou **Desligar** \n**Descrição:** Desliga a luz. \n\n";
      answer += "/Piscar ou **Piscar** \n**Descrição:** Irá fazer com que a luz pisque. \n\n";
      answer += "/Temperatura ou **Temperatura** \n**Descrição:** Informa a temperatura e umidade. \n\n";
    }
    else if (text == "Ligar" || text == "/Ligar") {
      digitalWrite(Rele, LOW);

      answer = from_name + " o dispositivo de SAÍDA 1 foi LIGADO ✔";
    }

    else if (text == "Desligar" || text == "/Desligar") {
      digitalWrite(Rele, HIGH);

      answer = from_name + " o dispositivo de SAÍDA 1 foi DESLIGADO ❌";
    }
    else if (text == "Piscar" || text == "/Piscar") {
      digitalWrite (Rele, HIGH); //Desliga
      digitalWrite (Rele, LOW); //Liga
      delay (200);
      digitalWrite (Rele, HIGH); //Desliga
      delay (500);
      digitalWrite (Rele, LOW); //Liga
      delay (200);
      digitalWrite (Rele, HIGH); //Desliga

      answer = "Feito! 😉";
    }
    else if (text == "Temperatura" || text == "/Temperatura") {
      float temperatura_lida = dht.readTemperature();
      float umidade_lida = dht.readHumidity();

      answer = "🌡 Temperatura: " + String(int(temperatura_lida)) + "ºC \n";
      answer += "💦 Umidade: " + String(int(umidade_lida)) + "%.";
    }
    else {
      answer = "Comando não aceito, por favor, tente novamente.";
      answer += "\n\nCaso não saiba o comando, digite(ou clique) /Comandos para saber os comandos disponiveis.";
    }
    Serial.println("Resposta para " + from_name + ": " + answer + "\n");
    bot.sendMessage(chatId, answer, "Markdown");
  }
}

boolean validateSender(String senderId)
{
  //Para cada id de usuário que pode interagir com este bot
  for (int i = 0; i < SENDER_ID_COUNT; i++)
  {
    //Se o id do remetente faz parte do array retornamos que é válido
    if (senderId == validSenderIds[i])
    {
      return true;
    }
  }
  //Se chegou aqui significa que verificou todos os ids e não encontrou no array
  return false;
}

void loop()
{
  {
    digitalWrite(LED_BUILTIN, LOW);
    delay(150);
    digitalWrite(LED_BUILTIN, HIGH);
    delay(150);
  }

  //Tempo agora desde o boot
  uint32_t now = millis();

  //Se o tempo passado desde a última checagem for maior que o intervalo determinado
  if (now - lastCheckTime >= Bot_mtbs){
    //Coloca o tempo de útlima checagem como agora e checa por mensagens
    lastCheckTime = now;
    int numNewMessages = bot.getUpdates(bot.last_message_received + 1);
    handleNewMessages(numNewMessages);
  }
  delay (400);
}
